# Fritzing sketch MorseAvecDiodeEtEcran (saved by Fritzing 0.9.3b)
breadboards: 1

parts:
  Composant1 = Arduino Uno (Rev3)
  S1 = Pushbutton [package="[SMD]"]
  LCD1 = LCD screen
  R1 = Rotary Potentiometer (Small) [maximum_resistance=100kΩ package=THT]
  R3 = Resistor [tolerance=±5% resistance=220 package=THT]
  R2 = Resistor [tolerance=±5% resistance=10k package=THT]
  LED1 = LED - 5mm [color="Red (633nm)" package="5 mm [THT]"]

nets:
  N1: Composant1.D10_PWM/SS, S1.Pin_3, S1.Pin_4
  N2: Composant1.D11_PWM/MOSI, LCD1.E
  N3: Composant1.D12/MISO, LCD1.RS
  GND: Composant1.GND, S1.Pin_1, S1.Pin_2, LCD1.VSS, LCD1.R/W, LCD1.LED-, R1.leg1, LED1.cathode
  N4: Composant1.D2, LCD1.DB7
  N5: Composant1.D3_PWM, LCD1.DB6
  N6: Composant1.D4, LCD1.DB5
  N7: Composant1.D5_PWM, LCD1.DB4
  N8: Composant1.D7, R2.Pin_1
  5V: Composant1.5V, LCD1.VDD, R1.leg2, R3.Pin_1
  N9: LCD1.V0, R1.wiper
  N10: LCD1.LED+, R3.Pin_0
  N11: R2.Pin_0, LED1.anode
